// Logisim project adapters.circ as structural Verilog
module dec_to_7seg (
  input  _0,
  input  _1,
  input  _2,
  input  _3,
  input  _4,
  input  _5,
  input  _6,
  input  _7,
  input  _8,
  input  _9,
  output right_bot,
  output bot,
  output left_bot,
  output mid,
  output left_top,
  output top,
  output right_top
);

  Transistor #(.\type ("n")) transistor_1 (.in(_0), .out(right_bot), .gate(_0));
  Transistor #(.\type ("n")) transistor_2 (.in(right_bot), .out(bot), .gate(_0));
  Transistor #(.\type ("n")) transistor_3 (.in(top), .out(left_top), .gate(_5));
  Transistor #(.\type ("n")) transistor_4 (.in(_5), .out(top), .gate(_5));
  Transistor #(.\type ("n")) transistor_5 (.in(left_bot), .out(left_top), .gate(_0));
  Transistor #(.\type ("n")) transistor_6 (.in(bot), .out(left_bot), .gate(_0));
  Transistor #(.\type ("n")) transistor_7 (.in(left_top), .out(mid), .gate(_5));
  Transistor #(.\type ("n")) transistor_8 (.in(mid), .out(bot), .gate(_5));
  Transistor #(.\type ("n")) transistor_9 (.in(left_top), .out(top), .gate(_0));
  Transistor #(.\type ("n")) transistor_10 (.in(top), .out(right_top), .gate(_0));
  Transistor #(.\type ("n")) transistor_11 (.in(bot), .out(right_bot), .gate(_5));
  Transistor #(.\type ("n")) transistor_12 (.in(_6), .out(left_top), .gate(_6));
  Transistor #(.\type ("n")) transistor_13 (.in(_1), .out(right_bot), .gate(_1));
  Transistor #(.\type ("n")) transistor_14 (.in(right_bot), .out(right_top), .gate(_1));
  Transistor #(.\type ("n")) transistor_15 (.in(mid), .out(left_bot), .gate(_6));
  Transistor #(.\type ("n")) transistor_16 (.in(left_top), .out(mid), .gate(_6));
  Transistor #(.\type ("n")) transistor_17 (.in(bot), .out(left_bot), .gate(_2));
  Transistor #(.\type ("n")) transistor_18 (.in(_2), .out(bot), .gate(_2));
  Transistor #(.\type ("n")) transistor_19 (.in(left_bot), .out(bot), .gate(_6));
  Transistor #(.\type ("n")) transistor_20 (.in(bot), .out(right_bot), .gate(_6));
  Transistor #(.\type ("n")) transistor_21 (.in(mid), .out(top), .gate(_2));
  Transistor #(.\type ("n")) transistor_22 (.in(left_bot), .out(mid), .gate(_2));
  Transistor #(.\type ("n")) transistor_23 (.in(right_top), .out(top), .gate(_7));
  Transistor #(.\type ("n")) transistor_24 (.in(_7), .out(right_top), .gate(_7));
  Transistor #(.\type ("n")) transistor_25 (.in(top), .out(right_top), .gate(_2));
  Transistor #(.\type ("n")) transistor_26 (.in(_3), .out(right_bot), .gate(_3));
  Transistor #(.\type ("n")) transistor_27 (.in(top), .out(right_bot), .gate(_7));
  Transistor #(.\type ("n")) transistor_28 (.in(right_bot), .out(bot), .gate(_3));
  Transistor #(.\type ("n")) transistor_29 (.in(bot), .out(mid), .gate(_3));
  Transistor #(.\type ("n")) transistor_30 (.in(right_top), .out(top), .gate(_8));
  Transistor #(.\type ("n")) transistor_31 (.in(_8), .out(right_top), .gate(_8));
  Transistor #(.\type ("n")) transistor_32 (.in(top), .out(right_top), .gate(_3));
  Transistor #(.\type ("n")) transistor_33 (.in(mid), .out(top), .gate(_3));
  Transistor #(.\type ("n")) transistor_34 (.in(left_top), .out(mid), .gate(_8));
  Transistor #(.\type ("n")) transistor_35 (.in(top), .out(left_top), .gate(_8));
  Transistor #(.\type ("n")) transistor_36 (.in(right_bot), .out(mid), .gate(_4));
  Transistor #(.\type ("n")) transistor_37 (.in(_4), .out(right_bot), .gate(_4));
  Transistor #(.\type ("n")) transistor_38 (.in(left_bot), .out(bot), .gate(_8));
  Transistor #(.\type ("n")) transistor_39 (.in(mid), .out(left_bot), .gate(_8));
  Transistor #(.\type ("n")) transistor_40 (.in(mid), .out(left_top), .gate(_4));
  Transistor #(.\type ("n")) transistor_41 (.in(left_top), .out(right_top), .gate(_4));
  Transistor #(.\type ("n")) transistor_42 (.in(bot), .out(right_bot), .gate(_8));
  Transistor #(.\type ("n")) transistor_43 (.in(_9), .out(right_top), .gate(_9));
  Transistor #(.\type ("n")) transistor_44 (.in(right_top), .out(top), .gate(_9));
  Transistor #(.\type ("n")) transistor_45 (.in(top), .out(left_top), .gate(_9));
  _7_Segment_Display u_7_segment_display_1 (
    .g(mid), .f(left_top), .a(top), .b(right_top), .e(left_bot), .d(bot), .c(right_bot));  // open: dp
  Transistor #(.\type ("n")) transistor_46 (.in(mid), .out(right_bot), .gate(_9));
  Transistor #(.\type ("n")) transistor_47 (.in(left_top), .out(mid), .gate(_9));
endmodule

module bin_to_7seg (
  input  in_1,
  input  in_2,
  input  in_3,
  input  in_4,
  output _0,
  output _1,
  output _2,
  output _3,
  output _4,
  output _5,
  output _6,
  output _7,
  output _8,
  output _9,
  output out_15
);

  wire and_1_out, and_2_out, and_3_out, and_4_out, and_5_out, and_6_out, and_7_out, and_8_out, and_9_out,
       and_10_out, and_11_out, and_12_out, and_13_out, and_14_out, and_15_out, and_16_out, dec_to_7seg_1_bot,
       dec_to_7seg_1_left_bot, dec_to_7seg_1_left_top, dec_to_7seg_1_mid, dec_to_7seg_1_right_bot,
       dec_to_7seg_1_right_top, dec_to_7seg_1_top, dec_to_7seg_2_bot, dec_to_7seg_2_left_bot,
       dec_to_7seg_2_left_top, dec_to_7seg_2_mid, dec_to_7seg_2_right_bot, dec_to_7seg_2_right_top,
       dec_to_7seg_2_top, not_1_out;

  and and_1 (and_1_out, in_4, ~in_3, ~in_2, ~in_1);  // AND_Gate
  and and_2 (and_2_out, ~in_4, ~in_3, ~in_2, ~in_1);  // AND_Gate
  or or_1 (_0, and_2_out, and_11_out);
  and and_3 (and_3_out, ~in_4, in_3, ~in_2, ~in_1);  // AND_Gate
  or or_2 (_1, and_1_out, and_12_out);
  or or_3 (_2, and_3_out, and_13_out);
  and and_4 (and_4_out, in_4, in_3, ~in_2, ~in_1);  // AND_Gate
  or or_4 (_3, and_4_out, and_14_out);
  and and_5 (and_5_out, ~in_4, ~in_3, in_2, ~in_1);  // AND_Gate
  and and_6 (and_6_out, in_4, ~in_3, in_2, ~in_1);  // AND_Gate
  or or_5 (_4, and_5_out, and_15_out);
  and and_7 (and_7_out, ~in_4, in_3, in_2, ~in_1);  // AND_Gate
  buf or_6 (_6, and_7_out);  // OR_Gate
  or or_7 (_5, and_6_out, and_16_out);
  and and_8 (and_8_out, in_4, in_3, in_2, ~in_1);  // AND_Gate
  buf or_8 (_7, and_8_out);  // OR_Gate
  and and_9 (and_9_out, ~in_4, ~in_3, ~in_2, in_1);  // AND_Gate
  and and_10 (and_10_out, in_4, ~in_3, ~in_2, in_1);  // AND_Gate
  buf or_9 (_8, and_9_out);  // OR_Gate
  and and_11 (and_11_out, ~in_4, in_3, ~in_2, in_1);  // AND_Gate
  buf or_10 (_9, and_10_out);  // OR_Gate
  and and_12 (and_12_out, in_4, in_3, ~in_2, in_1);  // AND_Gate
  or or_11 (out_15, and_11_out, and_12_out, and_13_out, and_14_out, and_15_out, and_16_out);
  and and_13 (and_13_out, in_4, in_3, ~in_2, ~in_1);  // AND_Gate
  and and_14 (and_14_out, ~in_4, in_3, ~in_2, in_1);  // AND_Gate
  not not_1 (not_1_out, out_15);
  dec_to_7seg dec_to_7seg_1 (
    ._0(not_1_out), ._1(out_15), ._2(1'b0), ._3(1'b0), ._4(1'b0), ._5(1'b0), ._6(1'b0), ._7(1'b0), ._8(1'b0),
    ._9(1'b0), .right_bot(dec_to_7seg_1_right_bot), .bot(dec_to_7seg_1_bot),
    .left_bot(dec_to_7seg_1_left_bot), .mid(dec_to_7seg_1_mid), .left_top(dec_to_7seg_1_left_top),
    .top(dec_to_7seg_1_top), .right_top(dec_to_7seg_1_right_top));
  dec_to_7seg dec_to_7seg_2 (
    ._0(_0), ._1(_1), ._2(_2), ._3(_3), ._4(_4), ._5(_5), ._6(_6), ._7(_7), ._8(_8), ._9(_9),
    .right_bot(dec_to_7seg_2_right_bot), .bot(dec_to_7seg_2_bot), .left_bot(dec_to_7seg_2_left_bot),
    .mid(dec_to_7seg_2_mid), .left_top(dec_to_7seg_2_left_top), .top(dec_to_7seg_2_top),
    .right_top(dec_to_7seg_2_right_top));
  and and_15 (and_15_out, ~in_4, in_3, in_2, in_1);  // AND_Gate
  and and_16 (and_16_out, in_4, in_3, in_2, in_1);
  _7_Segment_Display u_7_segment_display_1 (
    .g(dec_to_7seg_1_mid), .f(dec_to_7seg_1_left_top), .a(dec_to_7seg_1_top), .b(dec_to_7seg_1_right_top),
    .e(dec_to_7seg_1_left_bot), .d(dec_to_7seg_1_bot), .c(dec_to_7seg_1_right_bot));  // open: dp
  _7_Segment_Display u_7_segment_display_2 (
    .g(dec_to_7seg_2_mid), .f(dec_to_7seg_2_left_top), .a(dec_to_7seg_2_top), .b(dec_to_7seg_2_right_top),
    .e(dec_to_7seg_2_left_bot), .d(dec_to_7seg_2_bot), .c(dec_to_7seg_2_right_bot));  // open: dp
endmodule
